// Logisim project Lab3_cuellar.circ as structural Verilog
module onebitADDER (
  input  A,
  input  B,
  input  Cin,
  output S,
  output Cout
);

  wire and_1_out, and_2_out, and_3_out, and_4_out, and_5_out, and_6_out, and_7_out, not_1_out, not_2_out,
       not_3_out;

  not not_1 (not_1_out, A);
  not not_2 (not_2_out, B);
  not not_3 (not_3_out, Cin);
  and and_1 (and_1_out, not_1_out, not_2_out, Cin);
  and and_2 (and_2_out, not_1_out, B, not_3_out);
  and and_3 (and_3_out, A, not_2_out, not_3_out);
  and and_4 (and_4_out, A, B, Cin);
  and and_5 (and_5_out, B, Cin);
  and and_6 (and_6_out, Cin, A);
  and and_7 (and_7_out, A, B);
  or or_1 (S, and_1_out, and_2_out, and_3_out, and_4_out);
  or or_2 (Cout, and_5_out, and_6_out, and_7_out);
endmodule

module one_bit_ALU (
  input  [3:0] ALU_ctrl,
  input  A,
  input  B,
  input  C_in,
  output R,
  output C_out
);

  wire and_1_out, multiplexer_1_out, not_1_out, onebitadder_1_s, or_1_out, xor_1_out;

  not not_1 (not_1_out, B);
  Multiplexer #(.enable("false")) multiplexer_1 (.in0(B), .in1(not_1_out), .out(multiplexer_1_out), .sel(ALU_ctrl[2]));
  and and_1 (and_1_out, A, multiplexer_1_out);
  or or_1 (or_1_out, A, multiplexer_1_out);
  xor xor_1 (xor_1_out, A, multiplexer_1_out);
  onebitADDER onebitadder_1 (.A(A), .B(multiplexer_1_out), .Cin(C_in), .S(onebitadder_1_s), .Cout(C_out));
  Multiplexer #(.enable("false"), .select(2)) multiplexer_2 (
    .in0(and_1_out), .in1(or_1_out), .in2(xor_1_out), .in3(onebitadder_1_s), .out(R), .sel(ALU_ctrl[1:0]));
endmodule

module ALU_32_bits (
  input  [3:0] ALU_ctrl,
  input  [31:0] A,
  input  [31:0] B,
  output [31:0] R,
  output C_out
);

  wire alu_4_bits_1_c_out, alu_4_bits_2_c_out, alu_4_bits_3_c_out, alu_4_bits_4_c_out, alu_4_bits_5_c_out,
       alu_4_bits_6_c_out, alu_4_bits_7_c_out;
  wire [3:3] undriven;

  ALU_4_bits alu_4_bits_1 (
    .ALU_ctrl({undriven[3], ALU_ctrl[2:0]}), .A(A[3:0]), .B(B[3:0]), .R(R[3:0]), .C_out(alu_4_bits_1_c_out));  // open: C_in
  ALU_4_bits alu_4_bits_2 (
    .ALU_ctrl({undriven[3], ALU_ctrl[2:0]}), .A(A[7:4]), .B(B[7:4]), .C_in(alu_4_bits_1_c_out), .R(R[7:4]),
    .C_out(alu_4_bits_2_c_out));
  ALU_4_bits alu_4_bits_3 (
    .ALU_ctrl({undriven[3], ALU_ctrl[2:0]}), .A(A[11:8]), .B(B[11:8]), .C_in(alu_4_bits_2_c_out),
    .R(R[11:8]), .C_out(alu_4_bits_3_c_out));
  ALU_4_bits alu_4_bits_4 (
    .ALU_ctrl({undriven[3], ALU_ctrl[2:0]}), .A(A[15:12]), .B(B[15:12]), .C_in(alu_4_bits_3_c_out),
    .R(R[15:12]), .C_out(alu_4_bits_4_c_out));
  ALU_4_bits alu_4_bits_5 (
    .ALU_ctrl({undriven[3], ALU_ctrl[2:0]}), .A(A[19:16]), .B(B[19:16]), .C_in(alu_4_bits_4_c_out),
    .R(R[19:16]), .C_out(alu_4_bits_5_c_out));
  ALU_4_bits alu_4_bits_6 (
    .ALU_ctrl({undriven[3], ALU_ctrl[2:0]}), .A(A[23:20]), .B(B[23:20]), .C_in(alu_4_bits_5_c_out),
    .R(R[23:20]), .C_out(alu_4_bits_6_c_out));
  ALU_4_bits alu_4_bits_7 (
    .ALU_ctrl({undriven[3], ALU_ctrl[2:0]}), .A(A[27:24]), .B(B[27:24]), .C_in(alu_4_bits_6_c_out),
    .R(R[27:24]), .C_out(alu_4_bits_7_c_out));
  ALU_4_bits alu_4_bits_8 (
    .ALU_ctrl({undriven[3], ALU_ctrl[2:0]}), .A(A[31:28]), .B(B[31:28]), .C_in(alu_4_bits_7_c_out),
    .R(R[31:28]), .C_out(C_out));
endmodule

module ALU_4_bits (
  input  [3:0] ALU_ctrl,
  input  [3:0] A,
  input  [3:0] B,
  input  C_in,
  output [3:0] R,
  output C_out
);

  wire one_bit_alu_1_c_out, one_bit_alu_2_c_out, one_bit_alu_3_c_out;

  one_bit_ALU one_bit_alu_1 (
    .ALU_ctrl(ALU_ctrl), .A(A[0]), .B(B[0]), .C_in(C_in), .R(R[0]), .C_out(one_bit_alu_1_c_out));
  one_bit_ALU one_bit_alu_2 (
    .ALU_ctrl(ALU_ctrl), .A(A[1]), .B(B[1]), .C_in(one_bit_alu_1_c_out), .R(R[1]), .C_out(one_bit_alu_2_c_out));
  one_bit_ALU one_bit_alu_3 (
    .ALU_ctrl(ALU_ctrl), .A(A[2]), .B(B[2]), .C_in(one_bit_alu_2_c_out), .R(R[2]), .C_out(one_bit_alu_3_c_out));
  one_bit_ALU one_bit_alu_4 (
    .ALU_ctrl(ALU_ctrl), .A(A[3]), .B(B[3]), .C_in(one_bit_alu_3_c_out), .R(R[3]), .C_out(C_out));
endmodule

module register_file_32 (
  input  [31:0] WData,
  input  [4:0] RReg1,
  input  Clock_in,
  input  Write,
  input  [4:0] WReg,
  input  [4:0] RReg2,
  output [31:0] RData1,
  output [31:0] RData2
);

  wire r1, r2, r3, r4, r5, r6, r7, r8, r9, r10, r11, r12, r13, r14, r15, r16, r17, r18, r19, r20, r21, r22,
       r23, r24, r25, r26, r27, r28, r29, r30, r31, r32;
  wire [31:0] Q0, Q1, Q2, Q3, Q4, Q5, Q6, Q7, Q8, Q9, Q10, Q11, Q12, Q13, Q14, Q15, Q16, Q17, Q18, Q19, Q20,
       Q21, Q22, Q23, Q24, Q25, Q26, Q27, Q28, Q29, Q30, Q31;

  Demultiplexer #(.enable("false"), .select(5)) demultiplexer_1 (
    .out0(r1), .out1(r2), .out2(r3), .out3(r4), .out4(r5), .out5(r6), .out6(r7), .out7(r8), .out8(r9),
    .out9(r10), .out10(r11), .out11(r12), .out12(r13), .out13(r14), .out14(r15), .out15(r16), .out16(r17),
    .out17(r18), .out18(r19), .out19(r20), .out20(r21), .out21(r22), .out22(r23), .out23(r24), .out24(r25),
    .out25(r26), .out26(r27), .out27(r28), .out28(r29), .out29(r30), .out30(r31), .out31(r32), .in(Write),
    .sel(WReg));
  Register #(.width(32)) register_1 (.D(WData), .en(r1), .clk(Clock_in), .Q(Q0), .clr(Write));
  Register #(.width(32)) register_2 (.D(WData), .en(r2), .clk(Clock_in), .Q(Q1));  // open: clr
  Register #(.width(32)) register_3 (.D(WData), .en(r3), .clk(Clock_in), .Q(Q2));  // open: clr
  Register #(.width(32)) register_4 (.D(WData), .en(r4), .clk(Clock_in), .Q(Q3));  // open: clr
  Register #(.width(32)) register_5 (.D(WData), .en(r5), .clk(Clock_in), .Q(Q4));  // open: clr
  Register #(.width(32)) register_6 (.D(WData), .en(r6), .clk(Clock_in), .Q(Q5));  // open: clr
  Register #(.width(32)) register_7 (.D(WData), .en(r7), .clk(Clock_in), .Q(Q6));  // open: clr
  Register #(.width(32)) register_8 (.D(WData), .en(r8), .clk(Clock_in), .Q(Q7));  // open: clr
  Register #(.width(32)) register_9 (.D(WData), .en(r9), .clk(Clock_in), .Q(Q8));  // open: clr
  Register #(.width(32)) register_10 (.D(WData), .en(r10), .clk(Clock_in), .Q(Q9));  // open: clr
  Register #(.width(32)) register_11 (.D(WData), .en(r11), .clk(Clock_in), .Q(Q10));  // open: clr
  Register #(.width(32)) register_12 (.D(WData), .en(r12), .clk(Clock_in), .Q(Q11));  // open: clr
  Register #(.width(32)) register_13 (.D(WData), .en(r13), .clk(Clock_in), .Q(Q12));  // open: clr
  Register #(.width(32)) register_14 (.D(WData), .en(r14), .clk(Clock_in), .Q(Q13));  // open: clr
  Register #(.width(32)) register_15 (.D(WData), .en(r15), .clk(Clock_in), .Q(Q14));  // open: clr
  Register #(.width(32)) register_16 (.D(WData), .en(r16), .clk(Clock_in), .Q(Q15));  // open: clr
  Register #(.width(32)) register_17 (.D(WData), .en(r17), .clk(Clock_in), .Q(Q16));  // open: clr
  Register #(.width(32)) register_18 (.D(WData), .en(r18), .clk(Clock_in), .Q(Q17));  // open: clr
  Register #(.width(32)) register_19 (.D(WData), .en(r19), .clk(Clock_in), .Q(Q18));  // open: clr
  Register #(.width(32)) register_20 (.D(WData), .en(r20), .clk(Clock_in), .Q(Q19));  // open: clr
  Register #(.width(32)) register_21 (.D(WData), .en(r21), .clk(Clock_in), .Q(Q20));  // open: clr
  Register #(.width(32)) register_22 (.D(WData), .en(r22), .clk(Clock_in), .Q(Q21));  // open: clr
  Register #(.width(32)) register_23 (.D(WData), .en(r23), .clk(Clock_in), .Q(Q22));  // open: clr
  Register #(.width(32)) register_24 (.D(WData), .en(r24), .clk(Clock_in), .Q(Q23));  // open: clr
  Register #(.width(32)) register_25 (.D(WData), .en(r25), .clk(Clock_in), .Q(Q24));  // open: clr
  Register #(.width(32)) register_26 (.D(WData), .en(r26), .clk(Clock_in), .Q(Q25));  // open: clr
  Register #(.width(32)) register_27 (.D(WData), .en(r27), .clk(Clock_in), .Q(Q26));  // open: clr
  Register #(.width(32)) register_28 (.D(WData), .en(r28), .clk(Clock_in), .Q(Q27));  // open: clr
  Register #(.width(32)) register_29 (.D(WData), .en(r29), .clk(Clock_in), .Q(Q28));  // open: clr
  Register #(.width(32)) register_30 (.D(WData), .en(r30), .clk(Clock_in), .Q(Q29));  // open: clr
  Register #(.width(32)) register_31 (.D(WData), .en(r31), .clk(Clock_in), .Q(Q30));  // open: clr
  Register #(.width(32)) register_32 (.D(WData), .en(r32), .clk(Clock_in), .Q(Q31));  // open: clr
  Multiplexer #(.enable("false"), .select(5), .width(32)) multiplexer_1 (
    .out(RData1), .sel(RReg1));  // open: in0, in1, in2, in3, in4, in5, in6, in7, in8, in9, in10, in11, in12, in13, in14, in15, in16, in17, in18, in19, in20, in21, in22, in23, in24, in25, in26, in27, in28, in29, in30, in31
  Multiplexer #(.enable("false"), .select(5), .width(32)) multiplexer_2 (
    .out(RData2), .sel(RReg2));  // open: in0, in1, in2, in3, in4, in5, in6, in7, in8, in9, in10, in11, in12, in13, in14, in15, in16, in17, in18, in19, in20, in21, in22, in23, in24, in25, in26, in27, in28, in29, in30, in31
endmodule
